# Fritzing sketch SemaforoInteligente_v5.2 (saved by Fritzing 1.0.2b)
breadboards: 2

parts:
  LCM1602_IIC1 = LCM1602 IIC [part_number="LCM1602 IIC" chip_label="LCM1602 IIC" package="DIP (Dual Inline) [THT]"]
  Painel_automóveis = WS2812 RGB LED matrix 8x8
  Painel_pedestres = WS2812 RGB LED matrix 8x8
  SP1 = SPEAKER [package=pcb_mount_speaker]
  5V_10A = Power plug
  Componente1 = Standard LCD 16x2 white on blue [part_number=181]
  Buzzer = Active buzzer [package=THT]
  DFRobot_DFPlayer_Mini2 = DFRobot DFPlayer Mini [part_number=DFR0299]
  U1 = ESP32S-HiLetgo [part_number=ESP32S-HiLetgo]
  Botão = Tactile switch 12mm [package=THT]

nets:
  VSS: LCM1602_IIC1.VSS, Componente1.VSS
  VDD: LCM1602_IIC1.VDD, Componente1.VDD
  N1: LCM1602_IIC1.V0, Componente1.V0
  N2: LCM1602_IIC1.RS, Componente1.RS
  N3: LCM1602_IIC1.RW, Componente1.R/W
  N4: LCM1602_IIC1.E, Componente1.E
  N5: LCM1602_IIC1.D0, Componente1.DB0
  N6: LCM1602_IIC1.D1, Componente1.DB1
  N7: LCM1602_IIC1.D2, Componente1.DB2
  N8: LCM1602_IIC1.D3, Componente1.DB3
  N9: LCM1602_IIC1.D4, Componente1.DB4
  N10: LCM1602_IIC1.D5, Componente1.DB5
  N11: LCM1602_IIC1.D6, Componente1.DB6
  N12: LCM1602_IIC1.D7, Componente1.DB7
  N13: LCM1602_IIC1.A, Componente1.LED+
  N14: LCM1602_IIC1.K, Componente1.LED-
  GND: LCM1602_IIC1.GND, Buzzer.GND, DFRobot_DFPlayer_Mini2.GND-1, DFRobot_DFPlayer_Mini2.GND-2, U1.GND, Botão.1, Botão.2
  VCC: LCM1602_IIC1.VCC, DFRobot_DFPlayer_Mini2.VCC, U1.VIN
  N15: LCM1602_IIC1.SDA, U1.GPIO21
  N16: LCM1602_IIC1.SCL, U1.GPIO22
  N17: LCM1602_IIC1.LED_A, LCM1602_IIC1.LED_B
  GND_2: Painel_automóveis.GND, Painel_pedestres.GND, 5V_10A.GND
  VCC_2: Painel_automóveis.VCC, Painel_pedestres.VCC, 5V_10A.VCC
  N18: Painel_automóveis.DIN, U1.GPIO32
  N19: Painel_pedestres.DIN, U1.GPIO33
  N20: SP1.+, DFRobot_DFPlayer_Mini2.SPK_2
  N21: SP1.-, DFRobot_DFPlayer_Mini2.SPK_1
  N22: Buzzer.Vcc, U1.GPIO16
  N23: DFRobot_DFPlayer_Mini2.RX, U1.GPIO27
  N24: DFRobot_DFPlayer_Mini2.TX, U1.GPIO26
  N25: U1.GPIO17, Botão.3, Botão.4

custom parts:
  LCM1602 IIC: I2C-Module to use a 1602 or 2004 LCD on with the wire.h libory Serial LCD Modul
  WS2812 RGB LED matrix 8x8: WS2812 matrix 8x8
  Standard LCD 16x2 white on blue: Standard HD44780 LCDs are useful for creating standalone projects. * 16 characters wide, 2 rows * White text on blue background * Connection port is 0.1" pitch, single row for easy breadboarding and wiring
  Active buzzer: Active buzzer 12 mm, 3-5 V
  ESP32S-HiLetgo: HiLetgo ESP-WROOM-32 ESP32 ESP-32S Development Board 2.4GHz Dual-Mode WiFi + Bluetooth Dual Cores Microcontroller The ESP32 integrated with Antenna switches, RF Balun, power amplifiers, low-noise amplifiers, filters, and management modules, and the entire solution occupies the least area of PCB. 2.4 GHz Wi-Fi plus Bluetooth dual-mode chip, with TSMC Ultra-low power consumption 40nm technology,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
  Tactile switch 12mm: 12 mm tactile switch (push button/momentary switch) from the B3F family.
