# Fritzing sketch Rev4 (saved by Fritzing 1.0.1rc)
circuit board: 8.46667cm x 5.64444cm
breadboards: 1

parts:
  LED1 = LED - 5mm [color="Red (633nm)" current=0.030A package="5 mm [THT]"]
  R6 = Resistor [tolerance=±5% power=0.25W resistance=100 package=THT]
  LED2 = LED - 5mm [color="Yellow (585nm)" current=0.030A package="5 mm [THT]"]
  LED3 = LED - 5mm [color="Green (555nm)" current=0.030A package="5 mm [THT]"]
  LED4 = LED - 5mm [color="Red (633nm)" current=0.030A package="5 mm [THT]"]
  LED5 = LED - 5mm [color="Green (555nm)" current=0.030A package="5 mm [THT]"]
  R1 = Resistor [tolerance=±5% power=0.25W resistance=100 package=THT]
  R2 = Resistor [tolerance=±5% power=0.25W resistance=100 package=THT]
  R3 = Resistor [tolerance=±5% power=0.25W resistance=100 package=THT]
  R4 = Resistor [tolerance=±5% power=0.25W resistance=100 package=THT]
  Buzzer = Piezo Speaker
  LCD1 = LCD screen
  R5 = Resistor [tolerance=±5% power=0.25W resistance=100 package=THT]
  Arduino1 = Arduino Uno (Rev3)
  R7 = Resistor [tolerance=±5% power=0.25W resistance=100 package=THT]
  Botão = Pushbutton [package="[SMD]"]

nets:
  N1: LED1.cathode, R1.Pin_0
  N2: LED1.anode, Arduino1.D6_PWM
  VSS: R6.Pin_0, R1.Pin_1, R2.Pin_1, R3.Pin_1, R4.Pin_1, Buzzer.pin1, LCD1.VSS, LCD1.V0, LCD1.R/W, LCD1.LED-, R5.Pin_1, Arduino1.GND
  N3: R6.Pin_1, Botão.Pin_3, Botão.Pin_4
  N4: LED2.cathode, R2.Pin_0
  N5: LED2.anode, Arduino1.D5_PWM
  N6: LED3.cathode, R3.Pin_0
  N7: LED3.anode, Arduino1.D4
  N8: LED4.cathode, R4.Pin_0
  N9: LED4.anode, Arduino1.D3_PWM
  N10: LED5.cathode, R5.Pin_0
  N11: LED5.anode, Arduino1.D2
  N12: Buzzer.pin2, Arduino1.A0
  VDD: LCD1.VDD, Arduino1.5V, R7.Pin_0
  N13: LCD1.RS, Arduino1.D8
  N14: LCD1.E, Arduino1.D9_PWM
  N15: LCD1.DB4, Arduino1.D10_PWM/SS
  N16: LCD1.DB5, Arduino1.D11_PWM/MOSI
  N17: LCD1.DB6, Arduino1.D12/MISO
  N18: LCD1.DB7, Arduino1.D13/SCK
  N19: LCD1.LED+, R7.Pin_1
  N20: Arduino1.D7, Botão.Pin_1, Botão.Pin_2

notes:
  Semáforo Inteligente - Grupo 4, Protótipo funcional em hardware Arduino Uno R3, 4
